# Fritzing sketch ABOAVOBR_schematic (saved by Fritzing 0.9.3b)

parts:
  U1 = L298 [package=multiwatt15]
  M1 = DC Motor
  M2 = DC Motor
  USB_step_down_regulator = mystery part, 4 pins [chip_label=?]
  U2 = LIPO-2000mAh [package=lipo-2000]
  U3 = LIPO-2000mAh [package=lipo-2000]
  part = InvenSense MPU6050
  S1 = Square Pushbutton
  Part1 = Arduino Uno (Rev3) - ICSP

nets:
  N1: U1.OUT1, M1.pin_1
  N2: U1.OUT2, M1.pin_2
  N3: U1.VS, USB_step_down_regulator.pin1, U2.+
  N4: U1.IN1, Part1.D6_PWM
  N5: U1.ENA, Part1.D10_PWM/SS
  N6: U1.IN2, Part1.D7
  N7: U1.GND, USB_step_down_regulator.pin2, S1.leg0
  N8: U1.IN3, Part1.D5_PWM
  N9: U1.ENB, Part1.D9_PWM
  N10: U1.IN4, Part1.D4
  N11: U1.OUT3, M2.pin_1
  N12: U1.OUT4, M2.pin_2
  N13: U2.-, U3.+
  N14: U3.-, S1.leg1
  VCC: part.VCC, Part1.5V
  GND: part.GND, Part1.GND
  N15: part.SCL, Part1.A5/SCL
  N16: part.SDA, Part1.A4/SDA
